// Logisim project 5bitAdder.circ as structural Verilog
module FA (
  input  A,
  input  B,
  input  C,
  output Cout,
  output R
);

  wire and_1_out, and_2_out, and_3_out, and_4_out, and_5_out, and_6_out, and_7_out, not_1_out, not_2_out,
       not_3_out, not_4_out, not_5_out, not_6_out;

  and and_1 (and_1_out, B, C);
  and and_2 (and_2_out, A, C);
  and and_3 (and_3_out, A, B);
  not not_1 (not_1_out, A);
  not not_2 (not_2_out, B);
  not not_3 (not_3_out, A);
  not not_4 (not_4_out, C);
  not not_5 (not_5_out, B);
  not not_6 (not_6_out, C);
  or or_1 (Cout, and_1_out, and_2_out, and_3_out);
  and and_4 (and_4_out, not_1_out, not_2_out, C);
  and and_5 (and_5_out, not_3_out, B, not_4_out);
  and and_6 (and_6_out, A, not_5_out, not_6_out);
  and and_7 (and_7_out, A, B, C);
  or or_2 (R, and_4_out, and_5_out, and_6_out, and_7_out);
endmodule

module _5bitAdder (
  input  in_1,
  input  [4:0] A,
  input  [4:0] B,
  output [4:0] R,
  output Cout
);

  wire fa_1_cout, fa_2_cout, fa_3_cout, fa_4_cout;

  FA fa_1 (.A(A[0]), .B(B[0]), .C(in_1), .Cout(fa_1_cout), .R(R[0]));
  FA fa_2 (.A(A[1]), .B(B[1]), .C(fa_1_cout), .Cout(fa_2_cout), .R(R[1]));
  FA fa_3 (.A(A[2]), .B(B[2]), .C(fa_2_cout), .Cout(fa_3_cout), .R(R[2]));
  FA fa_4 (.A(A[3]), .B(B[3]), .C(fa_3_cout), .Cout(fa_4_cout), .R(R[3]));
  FA fa_5 (.A(A[4]), .B(B[4]), .C(fa_4_cout), .Cout(Cout), .R(R[4]));
endmodule
