// Logisim project COE301_project_Piplined.circ as structural Verilog
// Registers
module register_file (
  input  [2:0] RA,
  input  [2:0] RB,
  input  [2:0] RW,
  input  RegWrite,
  input  [15:0] BusW,
  input  in_6,
  input  clock,
  output [15:0] BusA,
  output [15:0] BusB
);

  wire and_1_out, and_2_out, and_3_out, and_4_out, and_5_out, and_6_out, and_7_out, decoder_1_out0,
       decoder_1_out1, decoder_1_out2, decoder_1_out3, decoder_1_out4, decoder_1_out5, decoder_1_out6,
       decoder_1_out7, decoder_2_out0, decoder_2_out1, decoder_2_out2, decoder_2_out3, decoder_2_out4,
       decoder_2_out5, decoder_2_out6, decoder_2_out7, decoder_3_out0, decoder_3_out1, decoder_3_out2,
       decoder_3_out3, decoder_3_out4, decoder_3_out5, decoder_3_out6, decoder_3_out7;
  wire [15:0] register_1_q, register_2_q, register_3_q, register_4_q, register_5_q, register_6_q,
       register_7_q;

  Decoder #(.select(3)) decoder_1 (
    .out0(decoder_1_out0), .out1(decoder_1_out1), .out2(decoder_1_out2), .out3(decoder_1_out3),
    .out4(decoder_1_out4), .out5(decoder_1_out5), .out6(decoder_1_out6), .out7(decoder_1_out7), .sel(RW));  // open: en
  and and_1 (and_1_out, decoder_1_out1, RegWrite);
  and and_2 (and_2_out, decoder_1_out2, RegWrite);
  and and_3 (and_3_out, decoder_1_out3, RegWrite);
  and and_4 (and_4_out, decoder_1_out4, RegWrite);
  and and_5 (and_5_out, decoder_1_out5, RegWrite);
  and and_6 (and_6_out, decoder_1_out6, RegWrite);
  and and_7 (and_7_out, decoder_1_out7, RegWrite);
  Register #(.width(16)) register_1 (.D(BusW), .en(and_1_out), .Q(register_1_q), .clk(clock), .clr(in_6));
  Register #(.width(16)) register_2 (.D(BusW), .en(and_2_out), .Q(register_2_q), .clk(clock), .clr(in_6));
  Register #(.width(16)) register_3 (.D(BusW), .en(and_3_out), .Q(register_3_q), .clk(clock), .clr(in_6));
  Register #(.width(16)) register_4 (.D(BusW), .en(and_4_out), .Q(register_4_q), .clk(clock), .clr(in_6));
  Register #(.width(16)) register_5 (.D(BusW), .en(and_5_out), .Q(register_5_q), .clk(clock), .clr(in_6));
  Register #(.width(16)) register_6 (.D(BusW), .en(and_6_out), .Q(register_6_q), .clk(clock), .clr(in_6));
  Register #(.width(16)) register_7 (.D(BusW), .en(and_7_out), .Q(register_7_q), .clk(clock), .clr(in_6));
  Decoder #(.select(3)) decoder_2 (
    .out0(decoder_2_out0), .out1(decoder_2_out1), .out2(decoder_2_out2), .out3(decoder_2_out3),
    .out4(decoder_2_out4), .out5(decoder_2_out5), .out6(decoder_2_out6), .out7(decoder_2_out7), .sel(RA));  // open: en
  assign BusA = decoder_2_out0 ? {16{1'b0}} : 16'bz;  // Controlled_Buffer controlled_buffer_1
  assign BusA = decoder_2_out1 ? register_1_q : 16'bz;  // Controlled_Buffer controlled_buffer_2
  assign BusA = decoder_2_out2 ? register_2_q : 16'bz;  // Controlled_Buffer controlled_buffer_3
  assign BusA = decoder_2_out3 ? register_3_q : 16'bz;  // Controlled_Buffer controlled_buffer_4
  assign BusA = decoder_2_out4 ? register_4_q : 16'bz;  // Controlled_Buffer controlled_buffer_5
  assign BusA = decoder_2_out5 ? register_5_q : 16'bz;  // Controlled_Buffer controlled_buffer_6
  assign BusA = decoder_2_out6 ? register_6_q : 16'bz;  // Controlled_Buffer controlled_buffer_7
  assign BusA = decoder_2_out7 ? register_7_q : 16'bz;  // Controlled_Buffer controlled_buffer_8
  Decoder #(.select(3)) decoder_3 (
    .out0(decoder_3_out0), .out1(decoder_3_out1), .out2(decoder_3_out2), .out3(decoder_3_out3),
    .out4(decoder_3_out4), .out5(decoder_3_out5), .out6(decoder_3_out6), .out7(decoder_3_out7), .sel(RB));  // open: en
  assign BusB = decoder_3_out0 ? {16{1'b0}} : 16'bz;  // Controlled_Buffer controlled_buffer_9
  assign BusB = decoder_3_out1 ? register_1_q : 16'bz;  // Controlled_Buffer controlled_buffer_10
  assign BusB = decoder_3_out2 ? register_2_q : 16'bz;  // Controlled_Buffer controlled_buffer_11
  assign BusB = decoder_3_out3 ? register_3_q : 16'bz;  // Controlled_Buffer controlled_buffer_12
  assign BusB = decoder_3_out4 ? register_4_q : 16'bz;  // Controlled_Buffer controlled_buffer_13
  assign BusB = decoder_3_out5 ? register_5_q : 16'bz;  // Controlled_Buffer controlled_buffer_14
  assign BusB = decoder_3_out6 ? register_6_q : 16'bz;  // Controlled_Buffer controlled_buffer_15
  assign BusB = decoder_3_out7 ? register_7_q : 16'bz;  // Controlled_Buffer controlled_buffer_16
endmodule

module ALU (
  input  [2:0] func,
  input  [15:0] A,
  input  [15:0] B,
  input  [3:0] OpCode,
  output BGT,
  output BGE,
  output BLT,
  output BLE,
  output MOVZ,
  output MOVN,
  output [15:0] ALU_Result,
  output Zero
);

  wire comparator_1_eq, comparator_1_gt, comparator_2_eq, comparator_2_gt, comparator_3_eq, comparator_4_gt,
       comparator_4_lt;
  wire [15:0] ADD, AND, bit_extender_1_out, bit_extender_2_out, bit_extender_3_out, bit_extender_4_out,
       multiplexer_1_out, multiplexer_2_out, nand_1_out, OR, or_2_out, or_3_out, shifter_1_out,
       shifter_2_out, shifter_3_out, shifter_4_out, shifter_5_out, SUB, xor_1_out, xor_2_out;

  assign xor_1_out = B ^ {16{1'b1}};  // XOR_Gate xor_1, 16 bits wide
  Adder #(.width(16)) adder_1 (.a(A), .b(xor_1_out), .out(SUB), .cin(1'b1));  // open: cout
  Adder #(.width(16)) adder_2 (.a(A), .b(B), .out(ADD), .cin(1'b0));  // open: cout
  Comparator #(.width(16)) comparator_1 (.a(A), .b(B), .gt(comparator_1_gt), .eq(comparator_1_eq));  // open: lt
  Comparator #(.width(16), .mode("unsigned")) comparator_2 (
    .a(A), .b(B), .gt(comparator_2_gt), .eq(comparator_2_eq));  // open: lt
  assign OR = A | B;  // OR_Gate or_1, 16 bits wide
  assign AND = A & B;  // AND_Gate and_1, 16 bits wide
  assign xor_2_out = A ^ B;  // XOR_Gate xor_2, 16 bits wide
  assign bit_extender_1_out = {{15{1'b0}}, comparator_1_gt};  // Bit_Extender bit_extender_1
  assign bit_extender_2_out = {{15{1'b0}}, comparator_1_eq};  // Bit_Extender bit_extender_2
  assign bit_extender_3_out = {{15{1'b0}}, comparator_2_gt};  // Bit_Extender bit_extender_3
  assign bit_extender_4_out = {{15{1'b0}}, comparator_2_eq};  // Bit_Extender bit_extender_4
  assign nand_1_out = ~(A & B);  // NAND_Gate nand_1, 16 bits wide
  assign or_2_out = bit_extender_1_out | bit_extender_2_out;  // OR_Gate or_2, 16 bits wide
  assign or_3_out = bit_extender_3_out | bit_extender_4_out;  // OR_Gate or_3, 16 bits wide
  Shifter #(.width(16)) shifter_1 (.in(A), .\dist (B[3:0]), .out(shifter_1_out));
  Shifter #(.width(16), .shift("lr")) shifter_2 (.in(A), .\dist (B[3:0]), .out(shifter_2_out));
  Shifter #(.width(16), .shift("ar")) shifter_3 (.in(A), .\dist (B[3:0]), .out(shifter_3_out));
  Shifter #(.width(16), .shift("rr")) shifter_4 (.in(A), .\dist (B[3:0]), .out(shifter_4_out));
  Shifter #(.width(16)) shifter_5 (.in(B), .\dist (4'b0100), .out(shifter_5_out));
  Multiplexer #(.select(3), .width(16)) multiplexer_1 (
    .in0(OR), .in1(AND), .in2(nand_1_out), .in3(xor_2_out), .in4(ADD), .in5(SUB), .in6(or_2_out),
    .in7(or_3_out), .out(multiplexer_1_out), .sel(func));  // open: en
  Multiplexer #(.select(3), .width(16)) multiplexer_2 (
    .in0(shifter_1_out), .in1(shifter_2_out), .in2(shifter_3_out), .in3(shifter_4_out), .in4(A), .in5(A),
    .in6({16{1'b0}}), .in7(B), .out(multiplexer_2_out), .sel(func));  // open: en
  Comparator #(.width(16)) comparator_3 (.a(A), .b(B), .gt(BGT), .eq(comparator_3_eq), .lt(BLT));
  Comparator #(.width(16)) comparator_4 (.a(B), .b({16{1'b0}}), .gt(comparator_4_gt), .eq(MOVZ), .lt(comparator_4_lt));
  Multiplexer #(.select(4), .width(16)) multiplexer_3 (
    .in0(multiplexer_1_out), .in1(multiplexer_2_out), .in2(AND), .in3(OR), .in4(ADD), .in5(ADD), .in6(ADD),
    .in7(SUB), .in8(SUB), .in9({16{1'b0}}), .in10({16{1'b0}}), .in11({16{1'b0}}), .in12({16{1'b0}}),
    .in13(shifter_5_out), .in14({16{1'b0}}), .in15(B), .out(ALU_Result), .sel(OpCode));  // open: en
  nor nor_1 (Zero, ALU_Result[15], ALU_Result[14], ALU_Result[13], ALU_Result[12], ALU_Result[11], ALU_Result[10], ALU_Result[9], ALU_Result[8], ALU_Result[7], ALU_Result[6], ALU_Result[5], ALU_Result[4], ALU_Result[3], ALU_Result[2], ALU_Result[1], ALU_Result[0]);
  or or_4 (MOVN, comparator_4_gt, comparator_4_lt);
  or or_5 (BGE, BGT, comparator_3_eq);
  or or_6 (BLE, BLT, comparator_3_eq);
endmodule

module PC_control (
  input  [2:0] func,
  input  Zero,
  input  [3:0] OpCode,
  input  [3:0] OpCode3,
  input  BGT,
  input  Branch,
  input  BGE,
  input  BLT,
  input  BLE,
  output kill1,
  output kill2,
  output [1:0] PCSrc
);

  wire comparator_1_eq, comparator_2_eq;
  wire [1:0] multiplexer_1_out, multiplexer_2_out, multiplexer_3_out, multiplexer_4_out, multiplexer_5_out,
       multiplexer_6_out, multiplexer_7_out;
  wire [3:0] multiplexer_9_out;

  Multiplexer #(.width(2), .enable("false")) multiplexer_1 (
    .in0(2'b10), .in1(2'b00), .out(multiplexer_1_out), .sel(Zero));
  Multiplexer #(.width(2), .enable("false")) multiplexer_2 (
    .in0(2'b00), .in1(2'b10), .out(multiplexer_2_out), .sel(Zero));
  Multiplexer #(.width(2), .enable("false")) multiplexer_3 (
    .in0(2'b00), .in1(2'b10), .out(multiplexer_3_out), .sel(BGT));
  Multiplexer #(.width(2), .enable("false")) multiplexer_4 (
    .in0(2'b00), .in1(2'b10), .out(multiplexer_4_out), .sel(BGE));
  Multiplexer #(.width(2), .enable("false")) multiplexer_5 (
    .in0(2'b00), .in1(2'b10), .out(multiplexer_5_out), .sel(BLT));
  Multiplexer #(.width(2), .enable("false")) multiplexer_6 (
    .in0(2'b00), .in1(2'b10), .out(multiplexer_6_out), .sel(BLE));
  Multiplexer #(.select(3), .width(2)) multiplexer_7 (
    .in0(2'b00), .in1(2'b00), .in2(2'b00), .in3(2'b00), .in4(2'b00), .in5(2'b00), .in6(2'b11), .in7(2'b11),
    .out(multiplexer_7_out), .sel(func));  // open: en
  Multiplexer #(.select(4), .width(2)) multiplexer_8 (
    .in0(2'b00), .in1(multiplexer_7_out), .in2(2'b00), .in3(2'b00), .in4(2'b00), .in5(2'b00), .in6(2'b00),
    .in7(multiplexer_1_out), .in8(multiplexer_2_out), .in9(multiplexer_3_out), .in10(multiplexer_4_out),
    .in11(multiplexer_5_out), .in12(multiplexer_6_out), .in13(2'b00), .in14(2'b01), .in15(2'b01),
    .out(PCSrc), .sel(multiplexer_9_out));  // open: en
  Multiplexer #(.width(4)) multiplexer_9 (
    .in0(OpCode), .in1(OpCode3), .out(multiplexer_9_out), .sel(Branch));  // open: en
  Comparator #(.width(2)) comparator_1 (.a(PCSrc), .b(2'b01), .eq(comparator_1_eq));  // open: gt, lt
  Comparator #(.width(2)) comparator_2 (.a(PCSrc), .b(2'b10), .eq(comparator_2_eq));  // open: gt, lt
  and and_1 (kill2, comparator_2_eq, Branch);
  or or_1 (kill1, comparator_1_eq, kill2);
endmodule

module single_cycle_CPU (
  input  in_1,
  input  in_2,
  input  in_3,
  output [15:0] out_4
);

  wire BGE, BGT, BLE, BLT, clock_1_out, ExtOp, main_control_1_memrd, main_control_1_memwr,
       main_control_1_regrb, main_control_1_regwrite, MOVN, MOVZ, Zero;
  wire [1:0] main_control_1_alusrc, main_control_1_regrd, main_control_1_wbdata, pc_control_1_p8;
  wire [2:0] func, multiplexer_2_out, multiplexer_3_out;
  wire [3:0] OpCode;
  wire [11:0] adder_2_out, multiplexer_1_out, PC_1, PC_q;
  wire [11:3] imm12;
  wire [15:0] alu_1_alu_result, bit_extender_1_out, bit_extender_2_out, bit_extender_3_out,
       bit_extender_4_out, multiplexer_5_out, multiplexer_6_out, RA, ram_1_data, register_file_1_busb;

  Multiplexer #(.select(2), .width(12)) multiplexer_1 (
    .in0(PC_1), .in1({imm12, func}), .in2(adder_2_out), .in3(RA[11:0]), .out(multiplexer_1_out),
    .sel(pc_control_1_p8));  // open: en
  // PC_control pc_control_1: pin names not known; wires that end beside it: Zero, BGT, BGE, BLT, BLE, OpCode, func, pc_control_1_p8
  Clock clock_1 (.out(clock_1_out));
  Register #(.width(12)) PC (.D(multiplexer_1_out), .Q(PC_q), .clk(clock_1_out), .clr(in_2));  // open: en
  Adder #(.width(12)) adder_1 (.a(PC_q), .b(12'h1), .out(PC_1), .cin(1'b0));  // open: cout
  ROM #(.addrWidth(12), .dataWidth(16)) rom_1 (.addr(PC_q), .data({OpCode, imm12, func}));  // open: sel
  main_control main_control_1 (
    .MOVN(MOVN), .MOVZ(MOVZ), .OpCode(OpCode), .RegRd(main_control_1_regrd), .RegRb(main_control_1_regrb),
    .func(func), .RegWrite(main_control_1_regwrite), .ExtOp(ExtOp), .ALUSrc(main_control_1_alusrc),
    .MemRd(main_control_1_memrd), .MemWr(main_control_1_memwr), .WBdata(main_control_1_wbdata));
  Multiplexer #(.width(3)) multiplexer_2 (
    .in0(imm12[5:3]), .in1(imm12[11:9]), .out(multiplexer_2_out), .sel(main_control_1_regrb));  // open: en
  Multiplexer #(.select(2), .width(3)) multiplexer_3 (
    .in0(imm12[11:9]), .in1(3'b001), .in2(3'b111), .out(multiplexer_3_out), .sel(main_control_1_regrd));  // open: in3, en
  assign bit_extender_1_out = {{10{1'b0}}, {imm12[5:3], func}};  // Bit_Extender bit_extender_1
  Multiplexer #(.width(16)) multiplexer_4 (
    .in0(bit_extender_1_out), .in1(bit_extender_2_out), .out(out_4), .sel(ExtOp));  // open: en
  assign bit_extender_2_out = {{10{imm12[5]}}, {imm12[5:3], func}};  // Bit_Extender bit_extender_2
  register_file register_file_1 (
    .RA(imm12[8:6]), .RB(multiplexer_2_out), .RW(multiplexer_3_out), .RegWrite(main_control_1_regwrite),
    .BusW(multiplexer_6_out), .BusA(RA), .BusB(register_file_1_busb), .clock(clock_1_out), .in_6(in_1));
  assign bit_extender_3_out = {{4{1'b0}}, {imm12, func}};  // Bit_Extender bit_extender_3
  Multiplexer #(.select(2), .width(16)) multiplexer_5 (
    .in0(register_file_1_busb), .in1(out_4), .in2(bit_extender_3_out), .out(multiplexer_5_out),
    .sel(main_control_1_alusrc));  // open: in3, en
  Adder #(.width(12)) adder_2 (.a(PC_1), .b(out_4[11:0]), .out(adder_2_out), .cin(1'b0));  // open: cout
  ALU alu_1 (
    .ALU_Result(alu_1_alu_result), .Zero(Zero), .A(RA), .B(multiplexer_5_out), .func(func), .OpCode(OpCode),
    .MOVZ(MOVZ), .MOVN(MOVN), .BGT(BGT), .BGE(BGE), .BLT(BLT), .BLE(BLE));
  RAM #(.addrWidth(12), .dataWidth(16), .bus("separate")) ram_1 (
    .addr(alu_1_alu_result[11:0]), .din(register_file_1_busb), .data(ram_1_data), .str(main_control_1_memwr),
    .clk(clock_1_out), .ld(main_control_1_memrd), .clr(in_3));  // open: sel
  Multiplexer #(.select(2), .width(16)) multiplexer_6 (
    .in0(alu_1_alu_result), .in1(ram_1_data), .in2(RA), .in3(bit_extender_4_out), .out(multiplexer_6_out),
    .sel(main_control_1_wbdata));  // open: en
  assign bit_extender_4_out = {{4{1'b0}}, PC_1};  // Bit_Extender bit_extender_4

  // Other names for the same wires on the sheet: imm12[2:0] = func

  // Notes on the sheet:
  //   contents of rom_1 (hex, n*v repeats v):
  //   4601 6dc 6dc b604 6400 5402 32c3 5200 2241 5200 0 e000
endmodule

module main_control (
  input  [2:0] func,
  input  MOVN,
  input  MOVZ,
  input  [3:0] OpCode,
  output [1:0] RegRd,
  output RegRb,
  output RegWrite,
  output ExtOp,
  output [1:0] ALUSrc,
  output MemRd,
  output MemWr,
  output [1:0] WBdata
);

  wire decoder_1_out1, decoder_1_out2, decoder_1_out3, decoder_1_out4, decoder_1_out7, decoder_1_out8,
       decoder_1_out9, decoder_1_out10, decoder_1_out11, decoder_1_out12, decoder_1_out14, decoder_2_out4,
       decoder_2_out5, decoder_2_out6, decoder_2_out7, JAL, JALR, JR, LUI, MOVN_t, MOVZ_t, multiplexer_4_out,
       multiplexer_5_out, multiplexer_8_out, nor_1_out, or_3_out, or_4_out, or_5_out;
  wire [1:0] bit_extender_1_out, multiplexer_1_out, multiplexer_2_out, multiplexer_6_out;

  Decoder #(.select(4), .enable("false")) decoder_1 (
    .out1(decoder_1_out1), .out2(decoder_1_out2), .out3(decoder_1_out3), .out4(decoder_1_out4), .out5(MemWr),
    .out6(MemRd), .out7(decoder_1_out7), .out8(decoder_1_out8), .out9(decoder_1_out9),
    .out10(decoder_1_out10), .out11(decoder_1_out11), .out12(decoder_1_out12), .out13(LUI),
    .out14(decoder_1_out14), .out15(JAL), .sel(OpCode));  // open: out0
  Decoder #(.select(3)) decoder_2 (
    .out4(decoder_2_out4), .out5(decoder_2_out5), .out6(decoder_2_out6), .out7(decoder_2_out7), .sel(func));  // open: out0, out1, out2, out3, en
  and and_1 (MOVZ_t, decoder_1_out1, decoder_2_out4);
  and and_2 (MOVN_t, decoder_1_out1, decoder_2_out5);
  and and_3 (JR, decoder_1_out1, decoder_2_out6);
  and and_4 (JALR, decoder_1_out1, decoder_2_out7);
  or or_1 (RegRb, MemWr, decoder_1_out7, decoder_1_out8, decoder_1_out9, decoder_1_out10, decoder_1_out11, decoder_1_out12);
  or or_2 (ExtOp, RegRb, decoder_1_out4, MemRd);
  nor nor_1 (nor_1_out, JR, RegRb, decoder_1_out14);
  or or_3 (or_3_out, MemWr, decoder_1_out4, MemRd, decoder_1_out2, decoder_1_out3);
  assign bit_extender_1_out = {{1{1'b0}}, or_3_out};  // Bit_Extender bit_extender_1
  Multiplexer #(.width(2)) multiplexer_1 (.in0(2'b00), .in1(2'b10), .out(multiplexer_1_out), .sel(JAL));  // open: en
  Multiplexer #(.width(2)) multiplexer_2 (.in0(2'b00), .in1(2'b01), .out(multiplexer_2_out), .sel(MemRd));  // open: en
  Multiplexer #(.width(2)) multiplexer_3 (.in0(multiplexer_1_out), .in1(2'b01), .out(RegRd), .sel(LUI));  // open: en
  Multiplexer multiplexer_4 (
    .in0(nor_1_out), .in1(multiplexer_5_out), .out(multiplexer_4_out), .sel(MOVN_t));  // open: en
  Multiplexer multiplexer_5 (.in0(1'b0), .in1(1'b1), .out(multiplexer_5_out), .sel(MOVN));  // open: en
  Multiplexer #(.width(2), .enable("false")) multiplexer_6 (
    .in0(multiplexer_2_out), .in1(2'b11), .out(multiplexer_6_out), .sel(or_4_out));
  or or_4 (or_4_out, JALR, JAL);
  Multiplexer multiplexer_7 (
    .in0(multiplexer_4_out), .in1(multiplexer_8_out), .out(RegWrite), .sel(MOVZ_t));  // open: en
  Multiplexer multiplexer_8 (.in0(1'b0), .in1(1'b1), .out(multiplexer_8_out), .sel(MOVZ));  // open: en
  Multiplexer #(.width(2)) multiplexer_9 (.in0(bit_extender_1_out), .in1(2'b10), .out(ALUSrc), .sel(LUI));  // open: en
  Multiplexer #(.width(2), .enable("false")) multiplexer_10 (
    .in0(multiplexer_6_out), .in1(2'b10), .out(WBdata), .sel(or_5_out));
  or or_5 (or_5_out, MOVZ_t, MOVN_t);
endmodule

module Pipelined_CPU (
  input  in_1,
  input  in_2,
  input  in_3
);

  wire BGE, BGT, BLE, BLT, Br, Clock, comparator_1_gt, comparator_2_lt, ExtOp, kill1, kill2,
       main_control_1_memrd, main_control_1_memwr, main_control_1_regrb, main_control_1_regwrite, MOVN, MOVZ,
       multiplexer_10_out, multiplexer_12_out, multiplexer_13_out, not_1_out, not_2_out, or_1_out,
       register_3_q, register_5_q, register_6_q, register_8_q, register_9_q, register_10_q, RegWr, Stall,
       Zero;
  wire [1:0] FoA, FoB, main_control_1_alusrc, main_control_1_regrd, main_control_1_wbdata,
       multiplexer_11_out, multiplexer_14_out, pc_control_1_pcsrc, register_4_q, register_7_q, register_11_q;
  wire [2:0] func, multiplexer_4_out, multiplexer_9_out, Rd2_q, Rd3_q, register_2_q, Rs, Rt, RW;
  wire [3:0] Branch, multiplexer_8_out, OpCode;
  wire [11:0] adder_1_out, adder_2_out, imm12, multiplexer_1_out, NPC_q, PC_1, PC_1_q, PC_q;
  wire [11:3] inst_q;
  wire [15:0] A_q, ALU_R, B_q, bit_extender_1_out, bit_extender_2_out, bit_extender_3_out,
       bit_extender_4_out, D_q, Data_q, Imm_q, multiplexer_2_out, multiplexer_5_out, multiplexer_6_out,
       multiplexer_7_out, multiplexer_15_out, R_q, RA, ram_1_data, register_file_1_busa,
       register_file_1_busb, rom_1_data, stage4;

  Multiplexer #(.select(2), .width(12)) multiplexer_1 (
    .in0(adder_1_out), .in1({inst_q[11:9], Rs, inst_q[5:3], func}), .in2(adder_2_out), .in3(RA[11:0]),
    .out(multiplexer_1_out), .sel(pc_control_1_pcsrc));  // open: en
  not not_1 (not_1_out, Stall);
  PC_control pc_control_1 (
    .OpCode(OpCode), .PCSrc(pc_control_1_pcsrc), .func(func), .Zero(Zero), .BGT(BGT), .BGE(BGE), .BLT(BLT),
    .BLE(BLE), .Branch(Br), .OpCode3(Branch), .kill1(kill1), .kill2(kill2));
  Comparator #(.width(4), .mode("unsigned")) comparator_1 (
    .a(Branch), .b(4'b0110), .gt(comparator_1_gt));  // open: eq, lt
  Comparator #(.width(4), .mode("unsigned")) comparator_2 (
    .a(Branch), .b(4'b1101), .lt(comparator_2_lt));  // open: gt, eq
  Register #(.width(12)) PC (.D(multiplexer_1_out), .en(not_1_out), .Q(PC_q), .clk(Clock), .clr(in_3));
  Clock clock_1 (.out(Clock));
  and and_1 (Br, comparator_1_gt, comparator_2_lt);
  Adder #(.width(12)) adder_1 (.a(PC_q), .b(12'h1), .out(adder_1_out), .cin(1'b0));  // open: cout
  Multiplexer #(.width(16)) multiplexer_2 (
    .in0(rom_1_data), .in1(16'h1), .out(multiplexer_2_out), .sel(kill1));  // open: en
  ROM #(.addrWidth(12), .dataWidth(16)) rom_1 (.addr(PC_q), .data(rom_1_data));  // open: sel
  not not_2 (not_2_out, Stall);
  Register #(.width(12)) NPC (.D(adder_1_out), .Q(NPC_q), .clk(Clock), .clr(in_3));  // open: en
  Register #(.width(16)) inst (
    .D(multiplexer_2_out), .en(not_2_out), .Q({OpCode, inst_q[11:9], Rs, inst_q[5:3], func}), .clk(Clock),
    .clr(in_3));
  main_control main_control_1 (
    .MOVN(MOVN), .MOVZ(MOVZ), .OpCode(OpCode), .RegRd(main_control_1_regrd), .RegRb(main_control_1_regrb),
    .func(func), .RegWrite(main_control_1_regwrite), .ExtOp(ExtOp), .ALUSrc(main_control_1_alusrc),
    .MemRd(main_control_1_memrd), .MemWr(main_control_1_memwr), .WBdata(main_control_1_wbdata));
  Multiplexer #(.width(3), .enable("false")) multiplexer_3 (
    .in0(inst_q[5:3]), .in1(inst_q[11:9]), .out(Rt), .sel(main_control_1_regrb));
  Multiplexer #(.select(2), .width(3), .enable("false")) multiplexer_4 (
    .in0(inst_q[11:9]), .in1(3'b001), .in2(3'b111), .out(multiplexer_4_out), .sel(main_control_1_regrd));  // open: in3
  assign bit_extender_1_out = {{10{1'b0}}, {inst_q[5:3], func}};  // Bit_Extender bit_extender_1
  assign bit_extender_2_out = {{10{inst_q[5]}}, {inst_q[5:3], func}};  // Bit_Extender bit_extender_2
  Multiplexer #(.width(16)) multiplexer_5 (
    .in0(bit_extender_1_out), .in1(bit_extender_2_out), .out(multiplexer_5_out), .sel(ExtOp));  // open: en
  register_file register_file_1 (
    .RA(Rs), .RB(Rt), .RW(RW), .RegWrite(RegWr), .BusW(Data_q), .BusA(register_file_1_busa),
    .BusB(register_file_1_busb), .clock(Clock), .in_6(in_1));
  or or_1 (or_1_out, kill2, Stall);
  Multiplexer #(.select(2), .width(16)) multiplexer_6 (
    .in0(register_file_1_busa), .in1(ALU_R), .in2(stage4), .in3(Data_q), .out(multiplexer_6_out), .sel(FoA));  // open: en
  Multiplexer #(.select(2), .width(16)) multiplexer_7 (
    .in0(register_file_1_busb), .in1(ALU_R), .in2(stage4), .in3(Data_q), .out(multiplexer_7_out), .sel(FoB));  // open: en
  Hazard_Detect___Forward hazard_detect_forward_1 (
    .Rs(Rs), .Rt(Rt), .Rd2(Rd2_q), .Rd3(Rd3_q), .Rd4(RW), .RegWr2(register_3_q), .RegWr3(register_8_q),
    .RegWr4(RegWr), .ForwardA(FoA), .ForwardB(FoB), .EX_MemRd(register_5_q), .Stall(Stall));
  Multiplexer #(.width(4)) multiplexer_8 (
    .in0(OpCode), .in1(4'b0000), .out(multiplexer_8_out), .sel(or_1_out));  // open: en
  Multiplexer #(.width(3)) multiplexer_9 (
    .in0(func), .in1(3'b000), .out(multiplexer_9_out), .sel(or_1_out));  // open: en
  Multiplexer multiplexer_10 (
    .in0(main_control_1_regwrite), .in1(1'b0), .out(multiplexer_10_out), .sel(or_1_out));  // open: en
  Multiplexer #(.width(2)) multiplexer_11 (
    .in0(main_control_1_alusrc), .in1(2'b00), .out(multiplexer_11_out), .sel(or_1_out));  // open: en
  Multiplexer multiplexer_12 (
    .in0(main_control_1_memrd), .in1(1'b0), .out(multiplexer_12_out), .sel(or_1_out));  // open: en
  Multiplexer multiplexer_13 (
    .in0(main_control_1_memwr), .in1(1'b0), .out(multiplexer_13_out), .sel(or_1_out));  // open: en
  Multiplexer #(.width(2)) multiplexer_14 (
    .in0(main_control_1_wbdata), .in1(2'b00), .out(multiplexer_14_out), .sel(or_1_out));  // open: en
  Register #(.width(12)) u_PC_1 (.D(adder_1_out), .Q(PC_1_q), .clk(Clock), .clr(in_3));  // open: en
  Register #(.width(12)) u_Imm12 (
    .D({inst_q[11:9], Rs, inst_q[5:3], func}), .Q(imm12), .clk(Clock), .clr(in_3));  // open: en
  Register #(.width(16)) Imm (.D(multiplexer_5_out), .Q(Imm_q), .clk(Clock), .clr(in_3));  // open: en
  Register #(.width(16)) A (.D(multiplexer_6_out), .Q(A_q), .clk(Clock), .clr(in_3));  // open: en
  Register #(.width(16)) B (.D(multiplexer_7_out), .Q(B_q), .clk(Clock), .clr(in_3));  // open: en
  Register #(.width(3)) Rd2 (.D(multiplexer_4_out), .Q(Rd2_q), .clk(Clock), .clr(in_3));  // open: en
  Register #(.width(4)) register_1 (.D(multiplexer_8_out), .Q(Branch), .clk(Clock), .clr(in_3));  // open: en
  Register #(.width(3)) register_2 (.D(multiplexer_9_out), .Q(register_2_q), .clk(Clock), .clr(in_3));  // open: en
  Register #(.width(1)) register_3 (.D(multiplexer_10_out), .Q(register_3_q), .clk(Clock), .clr(in_3));  // open: en
  Register #(.width(2)) register_4 (.D(multiplexer_11_out), .Q(register_4_q), .clk(Clock), .clr(in_3));  // open: en
  Register #(.width(1)) register_5 (.D(multiplexer_12_out), .Q(register_5_q), .clk(Clock), .clr(in_3));  // open: en
  Register #(.width(1)) register_6 (.D(multiplexer_13_out), .Q(register_6_q), .clk(Clock), .clr(in_3));  // open: en
  Register #(.width(2)) register_7 (.D(multiplexer_14_out), .Q(register_7_q), .clk(Clock), .clr(in_3));  // open: en
  Adder #(.width(12)) adder_2 (.a(NPC_q), .b(Imm_q[11:0]), .out(adder_2_out), .cin(1'b0));  // open: cout
  assign bit_extender_3_out = {{4{1'b0}}, imm12};  // Bit_Extender bit_extender_3
  Multiplexer #(.select(2), .width(16)) multiplexer_15 (
    .in0(B_q), .in1(Imm_q), .in2(bit_extender_3_out), .out(multiplexer_15_out), .sel(register_4_q));  // open: in3, en
  ALU alu_1 (
    .ALU_Result(ALU_R), .Zero(Zero), .A(A_q), .B(multiplexer_15_out), .func(register_2_q), .OpCode(Branch),
    .MOVZ(MOVZ), .MOVN(MOVN), .BGT(BGT), .BGE(BGE), .BLT(BLT), .BLE(BLE));
  Register #(.width(12)) PC_1_2 (.D(PC_1_q), .Q(PC_1), .clk(Clock), .clr(in_3));  // open: en
  Register #(.width(16)) u_RA (.D(A_q), .Q(RA), .clk(Clock), .clr(in_3));  // open: en
  Register #(.width(16)) R (.D(ALU_R), .Q(R_q), .clk(Clock), .clr(in_3));  // open: en
  Register #(.width(16)) D (.D(B_q), .Q(D_q), .clk(Clock), .clr(in_3));  // open: en
  Register #(.width(3)) Rd3 (.D(Rd2_q), .Q(Rd3_q), .clk(Clock), .clr(in_3));  // open: en
  Register #(.width(1)) register_8 (.D(register_3_q), .Q(register_8_q), .clk(Clock), .clr(in_3));  // open: en
  Register #(.width(1)) register_9 (.D(register_5_q), .Q(register_9_q), .clk(Clock), .clr(in_3));  // open: en
  Register #(.width(1)) register_10 (.D(register_6_q), .Q(register_10_q), .clk(Clock), .clr(in_3));  // open: en
  Register #(.width(2)) register_11 (.D(register_7_q), .Q(register_11_q), .clk(Clock), .clr(in_3));  // open: en
  RAM #(.addrWidth(12), .dataWidth(16), .bus("separate")) ram_1 (
    .addr(R_q[11:0]), .din(D_q), .data(ram_1_data), .str(register_10_q), .clk(Clock), .ld(register_9_q),
    .clr(in_2));  // open: sel
  Multiplexer #(.select(2), .width(16)) multiplexer_16 (
    .in0(R_q), .in1(ram_1_data), .in2(RA), .in3(bit_extender_4_out), .out(stage4), .sel(register_11_q));  // open: en
  assign bit_extender_4_out = {{4{1'b0}}, PC_1};  // Bit_Extender bit_extender_4
  Register #(.width(16)) Data (.D(stage4), .Q(Data_q), .clk(Clock), .clr(in_3));  // open: en
  Register #(.width(3)) Rd4 (.D(Rd3_q), .Q(RW), .clk(Clock), .clr(in_3));  // open: en
  Register #(.width(1)) register_12 (.D(register_8_q), .Q(RegWr), .clk(Clock), .clr(in_3));  // open: en

  // Other names for the same wires on the sheet: reset = in_3

  // Notes on the sheet:
  //   contents of rom_1 (hex, n*v repeats v):
  //   4601 6dc 6dc 5600 6400 5402 32c3 5200 2241 5200 8002 5201 0 0 e000 5201
endmodule

module Hazard_Detect___Forward (
  input  [2:0] Rs,
  input  [2:0] Rt,
  input  [2:0] Rd2,
  input  [2:0] Rd3,
  input  [2:0] Rd4,
  input  RegWr2,
  input  RegWr3,
  input  RegWr4,
  input  EX_MemRd,
  output [1:0] ForwardA,
  output [1:0] ForwardB,
  output Stall
);

  wire comparator_1_eq, comparator_2_eq, comparator_3_eq, comparator_4_eq, comparator_5_eq, comparator_6_eq,
       comparator_7_eq, comparator_8_eq, comparator_9_eq, comparator_10_eq, comparator_11_eq,
       comparator_12_eq, ForwardA1, ForwardA2, ForwardA3, ForwardB1, ForwardB2, ForwardB3, not_1_out,
       not_2_out, not_3_out, not_4_out, not_5_out, not_6_out, or_1_out;
  wire [1:0] multiplexer_1_out, multiplexer_2_out, multiplexer_3_out, multiplexer_4_out;

  Comparator #(.width(3)) comparator_1 (.a(3'b000), .b(Rs), .eq(comparator_1_eq));  // open: gt, lt
  Comparator #(.width(3)) comparator_2 (.a(Rs), .b(Rd2), .eq(comparator_2_eq));  // open: gt, lt
  Comparator #(.width(3)) comparator_3 (.a(3'b000), .b(Rs), .eq(comparator_3_eq));  // open: gt, lt
  Comparator #(.width(3)) comparator_4 (.a(Rs), .b(Rd3), .eq(comparator_4_eq));  // open: gt, lt
  Comparator #(.width(3)) comparator_5 (.a(3'b000), .b(Rs), .eq(comparator_5_eq));  // open: gt, lt
  Comparator #(.width(3)) comparator_6 (.a(Rs), .b(Rd4), .eq(comparator_6_eq));  // open: gt, lt
  Comparator #(.width(3)) comparator_7 (.a(3'b000), .b(Rt), .eq(comparator_7_eq));  // open: gt, lt
  Comparator #(.width(3)) comparator_8 (.a(Rt), .b(Rd2), .eq(comparator_8_eq));  // open: gt, lt
  Comparator #(.width(3)) comparator_9 (.a(3'b000), .b(Rt), .eq(comparator_9_eq));  // open: gt, lt
  Comparator #(.width(3)) comparator_10 (.a(Rt), .b(Rd3), .eq(comparator_10_eq));  // open: gt, lt
  Comparator #(.width(3)) comparator_11 (.a(3'b000), .b(Rt), .eq(comparator_11_eq));  // open: gt, lt
  Comparator #(.width(3)) comparator_12 (.a(Rt), .b(Rd4), .eq(comparator_12_eq));  // open: gt, lt
  not not_1 (not_1_out, comparator_1_eq);
  not not_2 (not_2_out, comparator_3_eq);
  not not_3 (not_3_out, comparator_5_eq);
  not not_4 (not_4_out, comparator_7_eq);
  not not_5 (not_5_out, comparator_9_eq);
  not not_6 (not_6_out, comparator_11_eq);
  and and_1 (ForwardA1, not_1_out, comparator_2_eq, RegWr2);
  and and_2 (ForwardA2, not_2_out, comparator_4_eq, RegWr3);
  and and_3 (ForwardA3, not_3_out, comparator_6_eq, RegWr4);
  and and_4 (ForwardB1, not_4_out, comparator_8_eq, RegWr2);
  and and_5 (ForwardB2, not_5_out, comparator_10_eq, RegWr3);
  and and_6 (ForwardB3, not_6_out, comparator_12_eq, RegWr4);
  Multiplexer #(.width(2)) multiplexer_1 (
    .in0(2'b00), .in1(2'b11), .out(multiplexer_1_out), .sel(ForwardA3));  // open: en
  Multiplexer #(.width(2)) multiplexer_2 (
    .in0(2'b00), .in1(2'b11), .out(multiplexer_2_out), .sel(ForwardB3));  // open: en
  Multiplexer #(.width(2)) multiplexer_3 (
    .in0(multiplexer_2_out), .in1(2'b10), .out(multiplexer_3_out), .sel(ForwardB2));  // open: en
  Multiplexer #(.width(2)) multiplexer_4 (
    .in0(multiplexer_1_out), .in1(2'b10), .out(multiplexer_4_out), .sel(ForwardA2));  // open: en
  or or_1 (or_1_out, ForwardA[0], ForwardB[0]);
  Multiplexer #(.width(2)) multiplexer_5 (
    .in0(multiplexer_4_out), .in1(2'b01), .out(ForwardA), .sel(ForwardA1));  // open: en
  Multiplexer #(.width(2)) multiplexer_6 (
    .in0(multiplexer_3_out), .in1(2'b01), .out(ForwardB), .sel(ForwardB1));  // open: en
  and and_7 (Stall, EX_MemRd, or_1_out);

  // Other names for the same wires on the sheet: ForA[1:0] = ForwardA; ForB[1:0] = ForwardB
endmodule
